// Logisim project 1.circ as structural Verilog: 2 circuits, main circuit TT_Clock1
module TT_Clock1 (
  input  Switch
);

  wire Clk_out, t_ff_1_qn, t_ff_2_qn, t_ff_3_qn;
  wire [3:0] t_ff_1_q;

  Clock #(.phaseOffset(1)) Clk (.out(Clk_out));
  T_Flip_Flop t_ff_1 (.T(Switch), .clk(Clk_out), .Q(t_ff_1_q[0]), .Qn(t_ff_1_qn));  // open: reset, preset
  T_Flip_Flop t_ff_2 (.T(Switch), .clk(t_ff_1_qn), .Q(t_ff_1_q[1]), .Qn(t_ff_2_qn));  // open: reset, preset
  T_Flip_Flop t_ff_3 (.T(Switch), .clk(t_ff_2_qn), .Q(t_ff_1_q[2]), .Qn(t_ff_3_qn));  // open: reset, preset
  T_Flip_Flop t_ff_4 (.T(Switch), .clk(t_ff_3_qn), .Q(t_ff_1_q[3]));  // open: Qn, reset, preset
  Hex_Digit_Display hex_digit_display_1 (.value(t_ff_1_q));  // open: dp
endmodule

module TT_Clock2 (
  input  Switch
);

  wire Clk_out;
  wire [3:0] Q0_q;

  Clock Clk (.out(Clk_out));
  T_Flip_Flop Q0 (.T(Switch), .clk(Clk_out), .Q(Q0_q[0]));  // open: Qn, reset, preset
  T_Flip_Flop Q1 (.T(Switch), .clk(Q0_q[0]), .Q(Q0_q[1]));  // open: Qn, reset, preset
  T_Flip_Flop Q2 (.T(Switch), .clk(Q0_q[1]), .Q(Q0_q[2]));  // open: Qn, reset, preset
  T_Flip_Flop Q3 (.T(Switch), .clk(Q0_q[2]), .Q(Q0_q[3]));  // open: Qn, reset, preset
  Hex_Digit_Display hex_digit_display_1 (.value(Q0_q));  // open: dp
endmodule
